# Fritzing sketch breath_openbci_schema (saved by Fritzing 0.8.5b)
breadboards: 1

parts:
  R2 = Resistor [tolerance=±5% resistance=33 part_number=R1 package=THT]
  R3 = Resistor [tolerance=±10% resistance=100 part_number=R3 package=THT]
  R4 = Resistor [tolerance=±10% resistance=22k part_number=R2 package=THT]
  R1 = Textile Stretch Sensor [part_number=PW052]

nets:
  N1: R2.Pin_1, R3.Pin_0, R4.Pin_0
  N2: R3.Pin_1, R1.pin_1

notes:
  Vin from OpenBCI, 3.3v
  about 30cm long, change R3 (22k) accordingly
  R1 at 33ohm and R2 at 100: voltage divider, from 3.3 to 2.5v
  Gnd from OpenBCI
  analog in
  Gnd to ref
