# Fritzing sketch breath_schema (saved by Fritzing 0.8.5b)
breadboards: 1

parts:
  U1 = INA128P [package=dip08]
  Composants1 = Arduino Due (Rev2b)
  R1 = Textile Stretch Sensor [part_number=PW052]
  U2 = POT [package=Custom]
  U3 = POT [package=Custom]

nets:
  N1: U1.GAIN#0, U3.S
  N2: U1.-IN, U1.V-
  N3: U1.+IN, R1.pin_1, U2.S
  N4: U1.Ref, Composants1.GND, R1.pin_0
  N5: U1.Vout, Composants1.A0
  N6: U1.V+, Composants1.IOREF, U2.E
  N7: U1.GAIN#7, U3.E

notes:
  could be a rubber stretch sensor instead
  adjust for 1v output at stretch baseline level
  adjust to get max output (2.3v) at max stretch

custom parts:
  INA128P: instrumental amplifier, quickly based on lm386 schematics
